# Fritzing sketch Esquematico_PanelHorario_v2-X-X (saved by Fritzing 0.9.3b)
breadboards: 1

parts:
  Componente1 = Arduino Mega ADK (Rev3)
  ZS-042_RTC1 = ZS-042 RTC Module
  S1 = Pushbutton [package=THT]
  MP3-1 = Serial MP3 Player
  S2 = Pushbutton [package=THT]
  S3 = Pushbutton [package=THT]
  S4 = Pushbutton [package=THT]
  S5 = Pushbutton [package=THT]
  S6 = Pushbutton [package=THT]
  S7 = Pushbutton [package=THT]
  S8 = Pushbutton [package=THT]
  S9 = Pushbutton [package=THT]
  S10 = Pushbutton [package=THT]
  U1_-_13_leds_-_Encendio_cuando_detecta_movimiento = WS2812 RGB LED strip
  U2_-_7_Leds_-_Día_de_la_semana = WS2812 RGB LED strip
  U3_-_55_leds_-_Franja_Horaria = WS2812 RGB LED strip
  R1 = Resistor [tolerance=±5% resistance=330 package=THT]
  R2 = Resistor [tolerance=±5% resistance=330 package=THT]
  R3 = Resistor [tolerance=±5% resistance=330 package=THT]
  PIR1 = PIR sensor

nets:
  N1: Componente1.D21/SCL, ZS-042_RTC1.SCL
  N2: Componente1.D20/SDA, ZS-042_RTC1.SDA
  N3: Componente1.D15/RX3, MP3-1.pin3
  N4: Componente1.D14/TX3, MP3-1.pin4
  VCC: Componente1.5V, ZS-042_RTC1.VCC, MP3-1.pin2, U1_-_13_leds_-_Encendio_cuando_detecta_movimiento.VCC, U2_-_7_Leds_-_Día_de_la_semana.VCC, U3_-_55_leds_-_Franja_Horaria.VCC, PIR1.VDD
  GND: Componente1.GND, ZS-042_RTC1.GND, S1.leg1, MP3-1.pin1, S2.leg1, S3.leg1, S4.leg1, S5.leg1, S6.leg1, S7.leg1, S8.leg1, S9.leg1, S10.leg1, U1_-_13_leds_-_Encendio_cuando_detecta_movimiento.GND, U2_-_7_Leds_-_Día_de_la_semana.GND, U3_-_55_leds_-_Franja_Horaria.GND, PIR1.GND
  N5: Componente1.D2_PWM, R1.Pin_0
  N6: Componente1.D3_PWM, R2.Pin_0
  N7: Componente1.D4_PWM, PIR1.SIG
  N8: Componente1.D5_PWM, R3.Pin_0
  N9: Componente1.D22, S1.leg0
  N10: Componente1.D23, S2.leg0
  N11: Componente1.D24, S3.leg0
  N12: Componente1.D25, S4.leg0
  N13: Componente1.D26, S5.leg0
  N14: Componente1.D27, S6.leg0
  N15: Componente1.D28, S7.leg0
  N16: Componente1.D29, S8.leg0
  N17: Componente1.D30, S9.leg0
  N18: Componente1.D31, S10.leg0
  N19: U1_-_13_leds_-_Encendio_cuando_detecta_movimiento.DIN, R1.Pin_1
  N20: U2_-_7_Leds_-_Día_de_la_semana.DIN, R2.Pin_1
  N21: U3_-_55_leds_-_Franja_Horaria.DIN, R3.Pin_1

custom parts:
  Serial MP3 Player: The module is a kind of simple MP3 player device which is based on a high-quality MP3 audio chip---YX5300. It can support 8k Hz ~ 48k Hz sampling frequency MP3 and WAV file formats. There is a TF card socket on board, so you can plug the micro SD card that stores audio files. MCU can control the MP3 playback state by sending commands to the module via UART port, such as switch songs, change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
  WS2812 RGB LED strip: WS2812 strip
